// Logisim project hw4.circ as structural Verilog: 5 circuits, main circuit main
module main (
  input  reset,
  input  [15:0] One,
  input  [15:0] in_3
);

  wire ChangePC, clk, Load, M1, undriven, WE;
  wire [1:0] NewPCSelect;
  wire [2:0] ALUOp, rd, rs, rt, shamt;
  wire [3:0] opcode;
  wire [5:0] imm;
  wire [11:0] j, PC;
  wire [15:0] adder_1_out, ALUResult, bit_extender_1_out, bPC, multiplexer_2_out, multiplexer_3_out, NewPC,
       RAMData, ReadData1, ReadData2, rom_1_data, rsPC, WriteData;
  wire [15:12] jPC;

  Clock clock_1 (.out(clk));
  Register #(.width(16)) u_PC (.D(multiplexer_3_out), .Q({jPC, PC}), .clk(clk), .clr(reset));  // open: en
  Multiplexer #(.select(2), .width(16), .enable("false")) multiplexer_1 (
    .in0({jPC, j}), .in1(bPC), .in2(rsPC), .out(NewPC), .sel(NewPCSelect));  // open: in3
  Adder #(.width(16)) adder_1 (.a(One), .b({jPC, PC}), .out(adder_1_out));  // open: cin, cout
  Multiplexer #(.width(16), .enable("false")) multiplexer_2 (
    .in0(ReadData2), .in1(bit_extender_1_out), .out(multiplexer_2_out), .sel(M1));
  assign bit_extender_1_out = {{10{imm[5]}}, imm};  // Bit_Extender bit_extender_1
  Multiplexer #(.width(16), .enable("false")) multiplexer_3 (
    .in0(adder_1_out), .in1(NewPC), .out(multiplexer_3_out), .sel(ChangePC));
  ALU ALU (.OpType(ALUOp), .op1(ReadData1), .op2(multiplexer_2_out), .shamt(shamt), .OutputData(ALUResult));
  Control control_1 (
    .op(opcode), .ALUOp(ALUOp), .NewPCSelect(NewPCSelect), .Load(Load), .ChangePC(ChangePC), .M1(M1));  // open: M2
  RegisterFile RegisterFile (
    .ReadReg1(rs), .ReadReg2(rt), .WriteReg(rd), .WriteData(WriteData), .RegWriteEnable(WE), .clk(clk),
    .Reset(reset), .ReadData1(ReadData1), .ReadData2(ReadData2));
  ROM #(.addrWidth(16), .dataWidth(16)) rom_1 (.addr({jPC, PC}), .data(rom_1_data));  // open: sel
  InstrDecoder InstrDecoder (
    .ROMInput(rom_1_data), .op(opcode), .rs(rs), .rt(rt), .rd(rd), .shamt(shamt), .j(j), .imm(imm));
  Multiplexer #(.width(16), .enable("false")) multiplexer_4 (
    .in0(ALUResult), .in1(RAMData), .out(WriteData), .sel(undriven));
  RAM #(.addrWidth(16), .dataWidth(16)) ram_1 (
    .addr(ALUResult), .data(RAMData), .clk(clk), .ld(Load), .clr(reset));  // open: sel

  // Other names for the same wires on the sheet: jPC[11:0] = j; PC[15:12] = jPC; res = reset

  // Notes on the sheet:
  //   contents of rom_1 (hex, n*v repeats v):
  //   1110
endmodule

module ALU (
  input  [2:0] OpType,
  input  [15:0] op1,
  input  [15:0] op2,
  input  [2:0] shamt,
  output [15:0] OutputData
);

  wire [3:0] bit_extender_1_out;
  wire [15:0] adder_1_out, not_1_out, shifter_1_out, shifter_2_out, subtractor_1_out, xor_1_out;

  assign bit_extender_1_out = {{1{1'b0}}, shamt};  // Bit_Extender bit_extender_1
  Adder #(.width(16)) adder_1 (.a(op1), .b(op2), .out(adder_1_out));  // open: cin, cout
  Subtractor #(.width(16)) subtractor_1 (.a(op1), .b(op2), .out(subtractor_1_out));  // open: bin, bout
  assign not_1_out = ~op1;  // NOT_Gate not_1, 16 bits wide
  assign xor_1_out = op1 ^ op2;  // XOR_Gate xor_1, 16 bits wide
  Shifter #(.width(16)) shifter_1 (.in(op1), .\dist (bit_extender_1_out), .out(shifter_1_out));
  Shifter #(.width(16), .shift("ar")) shifter_2 (.in(op1), .\dist (bit_extender_1_out), .out(shifter_2_out));
  Multiplexer #(.select(3), .width(16), .enable("false")) multiplexer_1 (
    .in0(adder_1_out), .in1(subtractor_1_out), .in2(not_1_out), .in3(xor_1_out), .in4(shifter_1_out),
    .in5(shifter_2_out), .out(OutputData), .sel(OpType));  // open: in6, in7

  // Other names for the same wires on the sheet: OT[2:0] = OpType
endmodule

module RegisterFile (
  input  [2:0] ReadReg1,
  input  [2:0] ReadReg2,
  input  [2:0] WriteReg,
  input  [15:0] WriteData,
  input  RegWriteEnable,
  input  clk,
  input  Reset,
  output [15:0] ReadData1,
  output [15:0] ReadData2
);

  wire and_1_out, and_2_out, and_3_out, and_4_out, and_5_out, and_6_out, and_7_out, and_8_out,
       decoder_1_out0, decoder_1_out1, decoder_1_out2, decoder_1_out3, decoder_1_out4, decoder_1_out5,
       decoder_1_out6, decoder_1_out7;
  wire [15:0] register_1_q, register_2_q, register_3_q, register_4_q, register_5_q, register_6_q,
       register_7_q, register_8_q;

  Decoder #(.select(3), .enable("false")) decoder_1 (
    .out0(decoder_1_out0), .out1(decoder_1_out1), .out2(decoder_1_out2), .out3(decoder_1_out3),
    .out4(decoder_1_out4), .out5(decoder_1_out5), .out6(decoder_1_out6), .out7(decoder_1_out7), .sel(WriteReg));
  and and_1 (and_1_out, decoder_1_out0, RegWriteEnable);
  and and_2 (and_2_out, decoder_1_out1, RegWriteEnable);
  and and_3 (and_3_out, decoder_1_out2, RegWriteEnable);
  and and_4 (and_4_out, decoder_1_out3, RegWriteEnable);
  and and_5 (and_5_out, decoder_1_out4, RegWriteEnable);
  and and_6 (and_6_out, decoder_1_out5, RegWriteEnable);
  and and_7 (and_7_out, decoder_1_out6, RegWriteEnable);
  and and_8 (and_8_out, decoder_1_out7, RegWriteEnable);
  Register #(.width(16), .trigger("falling")) register_1 (
    .D(WriteData), .en(and_1_out), .Q(register_1_q), .clk(clk), .clr(Reset));
  Register #(.width(16), .trigger("falling")) register_2 (
    .D(WriteData), .en(and_2_out), .Q(register_2_q), .clk(clk), .clr(Reset));
  Register #(.width(16), .trigger("falling")) register_3 (
    .D(WriteData), .en(and_3_out), .Q(register_3_q), .clk(clk), .clr(Reset));
  Register #(.width(16), .trigger("falling")) register_4 (
    .D(WriteData), .en(and_4_out), .Q(register_4_q), .clk(clk), .clr(Reset));
  Register #(.width(16), .trigger("falling")) register_5 (
    .D(WriteData), .en(and_5_out), .Q(register_5_q), .clk(clk), .clr(Reset));
  Register #(.width(16), .trigger("falling")) register_6 (
    .D(WriteData), .en(and_6_out), .Q(register_6_q), .clk(clk), .clr(Reset));
  Register #(.width(16), .trigger("falling")) register_7 (
    .D(WriteData), .en(and_7_out), .Q(register_7_q), .clk(clk), .clr(Reset));
  Register #(.width(16), .trigger("falling")) register_8 (
    .D(WriteData), .en(and_8_out), .Q(register_8_q), .clk(clk), .clr(Reset));
  // Probe on register_1_q
  // Probe on register_2_q
  // Probe on register_3_q
  // Probe on register_4_q
  // Probe on register_5_q
  // Probe on register_6_q
  // Probe on register_7_q
  // Probe on register_8_q
  Multiplexer #(.select(3), .width(16), .enable("false")) multiplexer_1 (
    .in0(register_1_q), .in1(register_2_q), .in2(register_3_q), .in3(register_4_q), .in4(register_5_q),
    .in5(register_6_q), .in6(register_7_q), .in7(register_8_q), .out(ReadData1), .sel(ReadReg1));
  Multiplexer #(.select(3), .width(16), .enable("false")) multiplexer_2 (
    .in0(register_1_q), .in1(register_2_q), .in2(register_3_q), .in3(register_4_q), .in4(register_5_q),
    .in5(register_6_q), .in6(register_7_q), .in7(register_8_q), .out(ReadData2), .sel(ReadReg2));

  // Other names for the same wires on the sheet: data[15:0] = WriteData; R1[2:0] = ReadReg1; R2[2:0] = ReadReg2;
  //   WE = RegWriteEnable
endmodule

module InstrDecoder (
  input  [15:0] ROMInput,
  output [3:0] op,
  output [2:0] rs,
  output [2:0] rt,
  output [2:0] rd,
  output [2:0] shamt,
  output [11:0] j,
  output [5:0] imm
);


  assign imm = ROMInput[5:0];
  assign j = ROMInput[11:0];
  assign op = ROMInput[15:12];
  assign rd = ROMInput[5:3];
  assign rs = ROMInput[11:9];
  assign rt = ROMInput[8:6];
  assign shamt = ROMInput[2:0];
endmodule

module Control (
  input  [3:0] op,
  output Load,
  output [2:0] ALUOp,
  output ChangePC,
  output [1:0] NewPCSelect,
  output M1,
  output M2
);

  wire add, Add_2_out, addi, and_1_out, and_2_out, and_3_out, and_4_out, blt, bne, branch_out, imm_out,
       \input , j, jal, jr, jump_out, lw, \not , or_2_out, or_3_out, or_4_out, or_5_out, \output , rt_out,
       sll, sra, sub, sw, \xor ;

  and u_not (\not , ~op[3], ~op[2], ~op[1], ~op[0]);  // AND_Gate
  and u_xor (\xor , ~op[3], ~op[2], ~op[1], op[0]);  // AND_Gate
  and u_add (add, ~op[3], ~op[2], op[1], op[0]);  // AND_Gate
  and u_addi (addi, ~op[3], ~op[2], op[1], ~op[0]);  // AND_Gate
  or Add_2 (Add_2_out, addi, add, lw, sw);
  or or_1 (ChangePC, blt, bne, jal, j, jr);
  or rt (rt_out, \xor , add, sub, blt, bne);
  or imm (imm_out, addi, lw, sw);
  and u_sub (sub, ~op[3], op[2], ~op[1], ~op[0]);  // AND_Gate
  and and_1 (and_1_out, ~Add_2_out, ~sub, ~\not , ~\xor , ~sra);  // AND_Gate
  and and_2 (and_2_out, ~rt_out, ~imm_out);  // AND_Gate
  // NOR_Gate nor_1 has open pins: out=M2
  and u_sra (sra, ~op[3], op[2], ~op[1], op[0]);  // AND_Gate
  or or_2 (or_2_out, Add_2_out, and_1_out);
  Priority_Encoder #(.disabled(0)) priority_encoder_1 (
    .in0(or_2_out), .in1(sub), .in2(\not ), .in3(\xor ), .in4(sll), .in5(sra), .out(ALUOp));  // open: in6, in7, en_in, gs, en_out
  or or_3 (or_3_out, rt_out, and_2_out);
  Priority_Encoder #(.select(1)) priority_encoder_2 (
    .in0(or_3_out), .in1(imm_out), .out(M1));  // open: gs, en_out, en_in
  and u_sll (sll, ~op[3], op[2], op[1], ~op[0]);  // AND_Gate
  and u_lw (lw, ~op[3], op[2], op[1], op[0]);  // AND_Gate
  and u_sw (sw, op[3], ~op[2], ~op[1], ~op[0]);  // AND_Gate
  and u_j (j, op[3], ~op[2], ~op[1], op[0]);  // AND_Gate
  and u_jr (jr, op[3], ~op[2], op[1], op[0]);  // AND_Gate
  and u_jal (jal, op[3], ~op[2], op[1], ~op[0]);  // AND_Gate
  and and_3 (and_3_out, ~sw, ~lw);  // AND_Gate
  or branch (branch_out, blt, bne);
  or jump (jump_out, jal, j);
  and and_4 (and_4_out, ~branch_out, ~jump_out, ~jr);  // AND_Gate
  and u_bne (bne, op[3], op[2], ~op[1], ~op[0]);  // AND_Gate
  Priority_Encoder #(.select(1)) priority_encoder_3 (.in0(or_4_out), .in1(lw), .out(Load));  // open: gs, en_out, en_in
  or or_4 (or_4_out, and_3_out, sw);
  and u_blt (blt, op[3], op[2], ~op[1], op[0]);  // AND_Gate
  or or_5 (or_5_out, and_4_out, branch_out);
  and u_input (\input , op[3], op[2], op[1], ~op[0]);  // AND_Gate
  and u_output (\output , op[3], op[2], op[1], op[0]);
  Priority_Encoder #(.select(2), .disabled(0)) priority_encoder_4 (
    .in0(or_5_out), .in1(jump_out), .in2(jr), .out(NewPCSelect));  // open: in3, gs, en_out, en_in
endmodule
